# Fritzing sketch Course Project (saved by Fritzing 0.9.3b)
breadboards: 2

parts:
  Part1 = Arduino Uno (Rev3) - ICSP
  hc-sr1 = hc-sr04
  J1 = Basic Servo
  U1 = LCD-16X2 [package=lcd-16x2]
  U2 = POT [package=pot_alpha_rv16af-20]
  R1 = Resistor [tolerance=±5% resistance=220 package="2512 [SMD]"]

nets:
  N1: Part1.D8, hc-sr1.Trig
  N2: Part1.D9_PWM, hc-sr1.Echo
  N3: Part1.D11_PWM/MOSI, U1.E
  N4: Part1.D12/MISO, U1.RS
  N5: Part1.D3_PWM, U1.DB7
  N6: Part1.D4, U1.DB6
  N7: Part1.D5_PWM, U1.DB5
  N8: Part1.D6_PWM, U1.DB4
  N9: Part1.D7, J1.pulse
  VCC: Part1.5V, hc-sr1.VCC, J1.vcc, U1.VDD, U2.A, R1.Pin_0
  GND: Part1.GND, hc-sr1.GND, J1.gnd, U1.R_W, U1.K
  N10: U1.VSS, U2.E
  N11: U1.VO, U2.S
  N12: U1.A, R1.Pin_1
